// Logisim project Project02.circ as structural Verilog
module Half_Adder (
  input  a,
  input  b,
  output sum,
  output carry
);

  xor xor_1 (sum, a, b);
  and and_1 (carry, a, b);
endmodule

module Full_Adder (
  input  a,
  input  b,
  input  c,
  output sum,
  output carry
);

  wire and_1_out, and_2_out, xor_1_out;

  xor xor_1 (xor_1_out, a, b);
  and and_1 (and_1_out, a, b);
  xor xor_2 (sum, xor_1_out, c);
  and and_2 (and_2_out, xor_1_out, c);
  or or_1 (carry, and_2_out, and_1_out);
endmodule
